# Fritzing sketch TSFRL_master_module (saved by Fritzing 0.9.0b)
circuit board: 9cm x 7cm
perfboards: 1

parts:
  KEYS_pins = rounded female pin header, 8 pins [form="♀ (female rounded)"]
  DATA/POWER_pins = male pin header, 5 pins [form="♂ (male)"]
  TEST = LED - 3mm [color="Blue (525nm)" current=20pA package="3 mm [THT]"]
  DATA = LED - 3mm [color="Yellow (595nm)" package="3 mm [THT]"]
  ERROR = LED - 3mm [color="Red (633nm)" package="3 mm [THT]"]
  DONE = LED - 3mm [color="Green (570nm)" package="3 mm [THT]"]
  ARDUINO_NANO = Arduino Nano (Rev3.0)
  R2 = Resistor [tolerance=±5% resistance=220 package=THT]
  R3 = Resistor [tolerance=±5% resistance=220 package=THT]
  R4 = Resistor [tolerance=±5% resistance=220 package=THT]
  R5 = Resistor [tolerance=±5% resistance=220 package=THT]
  LCD_pins = male pin header, 4 pins [form="♂ (male)"]
  IC2 = Hex Inverter Schmitt Trigger SN74HC14 [package="DIP (Dual Inline)"]
  U2 = DS75176BN [package=dil08]

nets:
  GND: KEYS_pins.pin1, DATA/POWER_pins.pin1, TEST.cathode, DATA.cathode, ERROR.cathode, DONE.cathode, ARDUINO_NANO.GND, LCD_pins.pin4, IC2.GND, U2.GND
  N1: KEYS_pins.pin2, DATA/POWER_pins.pin5, ARDUINO_NANO.RESET
  N2: KEYS_pins.pin3, IC2.3A
  N3: KEYS_pins.pin4, IC2.2A
  N4: KEYS_pins.pin5, IC2.1A
  N5: KEYS_pins.pin6, IC2.4A
  N6: KEYS_pins.pin7, IC2.5A
  5V: KEYS_pins.pin8, DATA/POWER_pins.pin4, ARDUINO_NANO.5V, LCD_pins.pin3, IC2.VCC, U2.VCC
  N7: DATA/POWER_pins.pin2, U2.DO/RI#5
  N8: DATA/POWER_pins.pin3, U2.DO/RI#6
  N9: TEST.anode, R5.Pin_1
  N10: DATA.anode, R2.Pin_1
  N11: ERROR.anode, R3.Pin_1
  N12: DONE.anode, R4.Pin_1
  N13: ARDUINO_NANO.D3, IC2.3Y
  N14: ARDUINO_NANO.D4, IC2.2Y
  N15: ARDUINO_NANO.D5, IC2.1Y
  N16: ARDUINO_NANO.D6, IC2.4Y
  N17: ARDUINO_NANO.D7, IC2.5Y
  N18: ARDUINO_NANO.D8, R5.Pin_0
  N19: ARDUINO_NANO.D9, R4.Pin_0
  N20: ARDUINO_NANO.D10, R3.Pin_0
  N21: ARDUINO_NANO.D11/MOSI, U2.DI
  N22: ARDUINO_NANO.D12/MISO, U2.RO
  N23: ARDUINO_NANO.A5, LCD_pins.pin1
  N24: ARDUINO_NANO.A4, LCD_pins.pin2
  N25: ARDUINO_NANO.D13/SCK, R2.Pin_0, U2.RE, U2.DE

notes:
  KEYS_pins
  1) +5v
  2) keyUP
  3) keyRIGHT
  4) keyLEFT
  5) keyDOWN
  6) keySTART
  7) keySTOP/CANCEL
  8) GND
  SDA(I2C)
  SCL(I2C)
  GND
  keySTOP/CANCEL
  keySTART
  keyDOWN
  keyLEFT
  keyRIGHT
  keyUP
  VCC +5V
  RESET signal
  RS485_a
  RS485_b
  Test Stand For Radio Lamps, Test Stand For Radio Lamps project: master module, 1.0
  LCD_pins
  1) SCL
  2) SDA
  3) +5v
  4) GND
  DATA/POWER_pins
  1) RESET signal
  2) +5v
  3) RS485_a
  4) RS485_b
  5) GND

custom parts:
  DS75176BN: RS-485 transceiver
