# Fritzing sketch TSFRL_slave_module (saved by Fritzing 0.9.0b)
circuit board: 9cm x 7cm
perfboards: 1

parts:
  DATA/POWER_pins = male pin header, 5 pins [form="♂ (male)"]
  DATA = LED - 3mm [color="Yellow (595nm)" package="3 mm [THT]"]
  ARDUINO_NANO = Arduino Nano (Rev3.0)
  R2 = Resistor [tolerance=±5% resistance=220 package=THT]
  U2 = DS75176BN [package=dil08]
  Q1 = NPN-Transistor [part_number=BC547B package="TO92 [THT]"]  # not connected
  R3 = Resistor [tolerance=±5% resistance=0 part_number=8,6k package=THT]  # not connected
  J1 = screw terminal, 3 pins  # not connected

nets:
  GND: DATA/POWER_pins.pin1, DATA.cathode, ARDUINO_NANO.GND, U2.GND
  N1: DATA/POWER_pins.pin2, U2.DO/RI#5
  N2: DATA/POWER_pins.pin3, U2.DO/RI#6
  5V: DATA/POWER_pins.pin4, ARDUINO_NANO.5V, U2.VCC
  N3: DATA/POWER_pins.pin5, ARDUINO_NANO.RESET
  N4: DATA.anode, R2.Pin_1
  N5: ARDUINO_NANO.D11/MOSI, U2.DI
  N6: ARDUINO_NANO.D12/MISO, U2.RO
  N7: ARDUINO_NANO.D13/SCK, R2.Pin_0, U2.RE, U2.DE

notes:
  GND
  VCC +5V
  RESET signal
  RS485_a
  RS485_b
  Test Stand For Radio Lamps, Test Stand For Radio Lamps project: slave module, 1.0
  DATA/POWER_pins
  1) RESET signal
  2) +5v
  3) RS485_a
  4) RS485_b
  5) GND

custom parts:
  DS75176BN: RS-485 transceiver
